// Logisim project proutiti.circ as structural Verilog: 1 circuit, main circuit main
module main (
  input  [7:0] A,
  input  [7:0] B,
  output [3:0] P
);

  and and_1 (P[0], A[0], B[0]);
endmodule
